// Logisim project 19_Moving Sign.circ as structural Verilog: 1 circuit, main circuit main
module main (
);

  wire clock_1_out, d_ff_1_q, d_ff_2_q, d_ff_3_q, d_ff_4_q, d_ff_5_q, d_ff_5_qn;

  LED led_1 (.in(d_ff_1_q));
  Clock clock_1 (.out(clock_1_out));
  LED led_2 (.in(d_ff_1_q));
  LED led_3 (.in(d_ff_1_q));
  D_Flip_Flop d_ff_1 (.clk(clock_1_out), .D(d_ff_5_qn), .Q(d_ff_1_q), .preset(1'b0), .reset(1'b0));  // open: Qn, en
  LED led_4 (.in(d_ff_2_q));
  LED led_5 (.in(d_ff_1_q));
  LED led_6 (.in(d_ff_2_q));
  D_Flip_Flop d_ff_2 (.clk(clock_1_out), .D(d_ff_1_q), .Q(d_ff_2_q), .preset(1'b0), .reset(1'b0));  // open: Qn, en
  LED led_7 (.in(d_ff_2_q));
  LED led_8 (.in(d_ff_3_q));
  LED led_9 (.in(d_ff_2_q));
  D_Flip_Flop d_ff_3 (.clk(clock_1_out), .D(d_ff_2_q), .Q(d_ff_3_q), .preset(1'b0), .reset(1'b0));  // open: Qn, en
  LED led_10 (.in(d_ff_3_q));
  LED led_11 (.in(d_ff_3_q));
  D_Flip_Flop d_ff_4 (.clk(clock_1_out), .D(d_ff_3_q), .Q(d_ff_4_q), .preset(1'b0), .reset(1'b0));  // open: Qn, en
  LED led_12 (.in(d_ff_4_q));
  LED led_13 (.in(d_ff_3_q));
  LED led_14 (.in(d_ff_4_q));
  D_Flip_Flop d_ff_5 (
    .clk(clock_1_out), .D(d_ff_4_q), .Q(d_ff_5_q), .Qn(d_ff_5_qn), .preset(1'b0), .reset(1'b0));  // open: en
  LED led_15 (.in(d_ff_4_q));
  LED led_16 (.in(d_ff_4_q));
  LED led_17 (.in(d_ff_5_q));
  LED led_18 (.in(d_ff_5_q));
  LED led_19 (.in(d_ff_5_q));
  LED led_20 (.in(d_ff_5_q));
  LED led_21 (.in(d_ff_5_q));
  LED led_22 (.in(d_ff_5_q));
  LED led_23 (.in(d_ff_5_q));
  LED led_24 (.in(d_ff_5_q));
  LED led_25 (.in(d_ff_5_q));
  LED led_26 (.in(d_ff_5_q));
  LED led_27 (.in(d_ff_5_q));
  LED led_28 (.in(d_ff_5_q));
  LED led_29 (.in(d_ff_5_q));
endmodule
