// Logisim project 22_Keyless Lock.circ as structural Verilog: 1 circuit, main circuit main
module main (
  input  S,
  input  S_2,
  input  S_3,
  input  S_4
);

  wire and_1_out, and_2_out, button_1_out, button_2_out, nor_1_out, nor_2_out, nor_3_out, nor_4_out,
       nor_5_out, nor_6_out, nor_7_out, nor_8_out, nor_9_out, nor_10_out, nor_11_out, nor_12_out;

  nor nor_1 (nor_1_out, S, nor_2_out);
  nor nor_2 (nor_2_out, nor_1_out, button_1_out);
  nor nor_3 (nor_3_out, S_2, nor_4_out);
  nor nor_4 (nor_4_out, nor_3_out, button_1_out);
  nor nor_5 (nor_5_out, S_3, nor_6_out);
  nor nor_6 (nor_6_out, nor_5_out, button_1_out);
  nor nor_7 (nor_7_out, S_4, nor_8_out);
  nor nor_8 (nor_8_out, nor_7_out, button_1_out);
  and and_1 (and_1_out, nor_2_out, nor_4_out, nor_6_out, nor_8_out);
  Button button_1 (.out(button_1_out));
  nor nor_9 (nor_9_out, and_1_out, nor_10_out);
  nor nor_10 (nor_10_out, nor_9_out, button_1_out);
  _7_Segment_Display u_7_segment_display_1 (
    .g(1'b0), .f(nor_12_out), .a(nor_12_out), .b(nor_12_out), .e(nor_12_out), .d(nor_12_out), .c(nor_12_out),
    .dp(1'b0));
  _7_Segment_Display u_7_segment_display_2 (
    .g(nor_12_out), .f(nor_12_out), .a(nor_12_out), .b(nor_12_out), .e(nor_12_out), .d(1'b0), .c(1'b0),
    .dp(1'b0));
  and and_2 (and_2_out, nor_10_out, button_1_out);
  _7_Segment_Display u_7_segment_display_3 (
    .g(nor_12_out), .f(nor_12_out), .a(nor_12_out), .b(1'b0), .e(nor_12_out), .d(nor_12_out), .c(1'b0),
    .dp(1'b0));
  Button button_2 (.out(button_2_out));
  _7_Segment_Display u_7_segment_display_4 (
    .g(1'b0), .f(nor_12_out), .a(nor_12_out), .b(nor_12_out), .e(nor_12_out), .d(1'b0), .c(nor_12_out),
    .dp(1'b0));
  nor nor_11 (nor_11_out, and_2_out, nor_12_out);
  nor nor_12 (nor_12_out, nor_11_out, button_2_out);

  // Notes on the sheet:
  //   R
  //   R
  //   R
  //   R
  //   ~Q
  //   Q
  //   ~Q
  //   Q
  //   ~Q
  //   Q
  //   ~Q
  //   Q
  //   S
  //   R
  //   ~Q
  //   Q
  //   S
  //   R
  //   ~Q
  //   Q
endmodule
