// Logisim project Car Alarm Example.circ as structural Verilog: 1 circuit, main circuit main
module main (
  input  Set,
  input  Reset,
  output out_3,
  output Q___ALARM,
  output Q___ALARM_2,
  output out_6
);

  nor nor_1 (out_3, Set, Q___ALARM);
  S_R_Flip_Flop s_r_ff_1 (.S(Set), .R(Reset), .Q(Q___ALARM_2), .Qn(out_6));  // open: clk, preset, reset, en
  nor nor_2 (Q___ALARM, out_3, Reset);

  // Notes on the sheet:
  //   ~Q - Armed and ready
  //   ~Q - Armed and ready
endmodule
