// Logisim project sr_ff as d_ff.circ as structural Verilog: 1 circuit, main circuit main
module main (
  input  in_1,
  output out_2,
  output out_3,
  output out_4,
  output out_5
);

  wire clock_1_out, not_1_out;

  not not_1 (not_1_out, in_1);
  D_Flip_Flop d_ff_1 (.clk(clock_1_out), .D(in_1), .Q(out_2), .Qn(out_3));  // open: preset, en, reset
  S_R_Flip_Flop s_r_ff_1 (
    .S(in_1), .clk(clock_1_out), .R(not_1_out), .Q(out_4), .Qn(out_5));  // open: preset, reset, en
  Clock clock_1 (.out(clock_1_out));

  // Notes on the sheet:
  //   SR_FF as D_FF
endmodule
